# Fritzing sketch Raspberry_Pi_Pwr_Button_On_Off_Diagram (saved by Fritzing 0.9.4)

parts:
  Mod1 = Raspberry Pi 4B
  J1 = Raspberry Pi Header 40pin [package=THT]  # not connected
  Mod2 = Raspberry Pi 4B
  J2 = Raspberry Pi Header 40pin [package=THT]  # not connected
  LED1 = LED - 5mm [color="Blue (430nm)" package="5 mm [THT]"]
  R1 = Resistor [tolerance=±5% resistance=330 package=THT]
  LED2 = LED - 5mm [color="Blue (430nm)" package="5 mm [THT]"]
  R2 = Resistor [tolerance=±5% resistance=330 package=THT]
  Mod3 = Raspberry Pi 4B
  LED3 = LED - 5mm [color="Blue (430nm)" package="5 mm [THT]"]
  R3 = Resistor [tolerance=±5% resistance=330 package=THT]
  J3 = Raspberry Pi Header 40pin [package=THT]  # not connected
  LED4 = LED - 5mm [color="Blue (430nm)" package="5 mm [THT]"]
  R4 = Resistor [tolerance=±5% resistance=330 package=THT]
  S4 = Square Pushbutton
  S2 = Square Pushbutton  # not connected
  S1 = Square Pushbutton
  S3 = Square Pushbutton  # not connected

nets:
  N1: Mod1.GPIO3, S1.leg0
  N2: Mod1.GND, S1.leg1
  N3: Mod2.GPIO14, LED1.anode
  N4: Mod2.GND, R1.Pin_1
  N5: LED1.cathode, R1.Pin_0
  N6: LED2.cathode, R2.Pin_0
  N7: Mod3.GPIO3, S4.leg0
  N8: Mod3.GPIO14, LED3.anode
  N9: Mod3.GND, R3.Pin_1, S4.leg1
  N10: LED3.cathode, R3.Pin_0
  N11: LED4.cathode, R4.Pin_0

custom parts:
  Raspberry Pi Header 40pin: Raspberry Pi 40 pin header - for creating your own shields. (Mar 2020, bb: make breadboard friendly (.4in pin spacing) and add labels. Schematic add labels. PCB make oblong pins to allow routing traces between the pins.)
